// Logisim project Rigister32.circ as structural Verilog: 1 circuit, main circuit Rigisters
module Rigisters (
  input  RegWrite,
  input  [31:0] Data2Reg,
  input  Clock,
  input  [4:0] Rs5Bit,
  input  [4:0] Rt5Bit,
  input  [4:0] Rd5Bit,
  output [31:0] RD1,
  output [31:0] RD2
);

  wire decoder_1_out1, decoder_1_out2, decoder_1_out3, decoder_1_out4, decoder_1_out5, decoder_1_out6,
       decoder_1_out7, decoder_1_out8, decoder_1_out9, decoder_1_out10, decoder_1_out11, decoder_1_out12,
       decoder_1_out13, decoder_1_out14, decoder_1_out15, decoder_1_out16, decoder_1_out17, decoder_1_out18,
       decoder_1_out19, decoder_1_out20, decoder_1_out21, decoder_1_out22, decoder_1_out23, decoder_1_out24,
       decoder_1_out25, decoder_1_out26, decoder_1_out27, decoder_1_out28, decoder_1_out29, decoder_1_out30,
       decoder_1_out31, WE1, WE2, WE3, WE4, WE5, WE6, WE7, WE8, WE9, WE10, WE11, WE12, WE13, WE14, WE15,
       WE16, WE17, WE18, WE19, WE20, WE21, WE22, WE23, WE24, WE25, WE26, WE27, WE28, WE29, WE30, WE31;
  wire [31:0] REG1, REG2, REG3, REG4, REG5, REG6, REG7, REG8, REG9, REG10, REG11, REG12, REG13, REG14, REG15,
       REG16, REG17, REG18, REG19, REG20, REG21, REG22, REG23, REG24, REG25, REG26, REG27, REG28, REG29,
       REG30, REG31;

  Register #(.width(32)) register_1 (.D(Data2Reg), .en(WE1), .clk(Clock), .Q(REG1), .clr(1'b0));
  Register #(.width(32)) register_2 (.D(Data2Reg), .en(WE2), .clk(Clock), .Q(REG2), .clr(1'b0));
  Register #(.width(32)) register_3 (.D(Data2Reg), .en(WE3), .clk(Clock), .Q(REG3), .clr(1'b0));
  Register #(.width(32)) register_4 (.D(Data2Reg), .en(WE4), .clk(Clock), .Q(REG4), .clr(1'b0));
  Register #(.width(32)) register_5 (.D(Data2Reg), .en(WE5), .clk(Clock), .Q(REG5), .clr(1'b0));
  Register #(.width(32)) register_6 (.D(Data2Reg), .en(WE6), .clk(Clock), .Q(REG6), .clr(1'b0));
  Register #(.width(32)) register_7 (.D(Data2Reg), .en(WE7), .clk(Clock), .Q(REG7), .clr(1'b0));
  Register #(.width(32)) register_8 (.D(Data2Reg), .en(WE8), .clk(Clock), .Q(REG8), .clr(1'b0));
  Register #(.width(32)) register_9 (.D(Data2Reg), .en(WE9), .clk(Clock), .Q(REG9), .clr(1'b0));
  Register #(.width(32)) register_10 (.D(Data2Reg), .en(WE10), .clk(Clock), .Q(REG10), .clr(1'b0));
  Register #(.width(32)) register_11 (.D(Data2Reg), .en(WE11), .clk(Clock), .Q(REG11), .clr(1'b0));
  Register #(.width(32)) register_12 (.D(Data2Reg), .en(WE12), .clk(Clock), .Q(REG12), .clr(1'b0));
  Register #(.width(32)) register_13 (.D(Data2Reg), .en(WE13), .clk(Clock), .Q(REG13), .clr(1'b0));
  Register #(.width(32)) register_14 (.D(Data2Reg), .en(WE14), .clk(Clock), .Q(REG14), .clr(1'b0));
  Register #(.width(32)) register_15 (.D(Data2Reg), .en(WE15), .clk(Clock), .Q(REG15), .clr(1'b0));
  Register #(.width(32)) register_16 (.D(Data2Reg), .en(WE16), .clk(Clock), .Q(REG16), .clr(1'b0));
  Register #(.width(32)) register_17 (.D(Data2Reg), .en(WE17), .clk(Clock), .Q(REG17), .clr(1'b0));
  Register #(.width(32)) register_18 (.D(Data2Reg), .en(WE18), .clk(Clock), .Q(REG18), .clr(1'b0));
  Register #(.width(32)) register_19 (.D(Data2Reg), .en(WE19), .clk(Clock), .Q(REG19), .clr(1'b0));
  Register #(.width(32)) register_20 (.D(Data2Reg), .en(WE20), .clk(Clock), .Q(REG20), .clr(1'b0));
  Register #(.width(32)) register_21 (.D(Data2Reg), .en(WE21), .clk(Clock), .Q(REG21), .clr(1'b0));
  Register #(.width(32)) register_22 (.D(Data2Reg), .en(WE22), .clk(Clock), .Q(REG22), .clr(1'b0));
  Register #(.width(32)) register_23 (.D(Data2Reg), .en(WE23), .clk(Clock), .Q(REG23), .clr(1'b0));
  Register #(.width(32)) register_24 (.D(Data2Reg), .en(WE24), .clk(Clock), .Q(REG24), .clr(1'b0));
  Register #(.width(32)) register_25 (.D(Data2Reg), .en(WE25), .clk(Clock), .Q(REG25), .clr(1'b0));
  Register #(.width(32)) register_26 (.D(Data2Reg), .en(WE26), .clk(Clock), .Q(REG26), .clr(1'b0));
  Register #(.width(32)) register_27 (.D(Data2Reg), .en(WE27), .clk(Clock), .Q(REG27), .clr(1'b0));
  Register #(.width(32)) register_28 (.D(Data2Reg), .en(WE28), .clk(Clock), .Q(REG28), .clr(1'b0));
  Register #(.width(32)) register_29 (.D(Data2Reg), .en(WE29), .clk(Clock), .Q(REG29), .clr(1'b0));
  Register #(.width(32)) register_30 (.D(Data2Reg), .en(WE30), .clk(Clock), .Q(REG30), .clr(1'b0));
  Register #(.width(32)) register_31 (.D(Data2Reg), .en(WE31), .clk(Clock), .Q(REG31), .clr(1'b0));
  Multiplexer #(.select(5), .width(32)) multiplexer_1 (
    .in0({32{1'b0}}), .in1(REG1), .in2(REG2), .in3(REG3), .in4(REG4), .in5(REG5), .in6(REG6), .in7(REG7),
    .in8(REG8), .in9(REG9), .in10(REG10), .in11(REG11), .in12(REG12), .in13(REG13), .in14(REG14),
    .in15(REG15), .in16(REG16), .in17(REG17), .in18(REG18), .in19(REG19), .in20(REG20), .in21(REG21),
    .in22(REG22), .in23(REG23), .in24(REG24), .in25(REG25), .in26(REG26), .in27(REG27), .in28(REG28),
    .in29(REG29), .in30(REG30), .in31(REG31), .out(RD1), .sel(Rs5Bit));
  Multiplexer #(.select(5), .width(32)) multiplexer_2 (
    .in0({32{1'b0}}), .in1(REG1), .in2(REG2), .in3(REG3), .in4(REG4), .in5(REG5), .in6(REG6), .in7(REG7),
    .in8(REG8), .in9(REG9), .in10(REG10), .in11(REG11), .in12(REG12), .in13(REG13), .in14(REG14),
    .in15(REG15), .in16(REG16), .in17(REG17), .in18(REG18), .in19(REG19), .in20(REG20), .in21(REG21),
    .in22(REG22), .in23(REG23), .in24(REG24), .in25(REG25), .in26(REG26), .in27(REG27), .in28(REG28),
    .in29(REG29), .in30(REG30), .in31(REG31), .out(RD2), .sel(Rt5Bit));
  and and_1 (WE1, decoder_1_out1, RegWrite);
  and and_2 (WE2, decoder_1_out2, RegWrite);
  and and_3 (WE3, decoder_1_out3, RegWrite);
  and and_4 (WE4, decoder_1_out4, RegWrite);
  and and_5 (WE5, decoder_1_out5, RegWrite);
  and and_6 (WE6, decoder_1_out6, RegWrite);
  and and_7 (WE7, decoder_1_out7, RegWrite);
  and and_8 (WE8, decoder_1_out8, RegWrite);
  and and_9 (WE9, decoder_1_out9, RegWrite);
  and and_10 (WE10, decoder_1_out10, RegWrite);
  and and_11 (WE11, decoder_1_out11, RegWrite);
  and and_12 (WE12, decoder_1_out12, RegWrite);
  and and_13 (WE13, decoder_1_out13, RegWrite);
  and and_14 (WE14, decoder_1_out14, RegWrite);
  and and_15 (WE15, decoder_1_out15, RegWrite);
  and and_16 (WE16, decoder_1_out16, RegWrite);
  and and_17 (WE17, decoder_1_out17, RegWrite);
  and and_18 (WE18, decoder_1_out18, RegWrite);
  and and_19 (WE19, decoder_1_out19, RegWrite);
  and and_20 (WE20, decoder_1_out20, RegWrite);
  and and_21 (WE21, decoder_1_out21, RegWrite);
  and and_22 (WE22, decoder_1_out22, RegWrite);
  and and_23 (WE23, decoder_1_out23, RegWrite);
  and and_24 (WE24, decoder_1_out24, RegWrite);
  and and_25 (WE25, decoder_1_out25, RegWrite);
  and and_26 (WE26, decoder_1_out26, RegWrite);
  and and_27 (WE27, decoder_1_out27, RegWrite);
  and and_28 (WE28, decoder_1_out28, RegWrite);
  and and_29 (WE29, decoder_1_out29, RegWrite);
  and and_30 (WE30, decoder_1_out30, RegWrite);
  and and_31 (WE31, decoder_1_out31, RegWrite);
  Decoder #(.select(5)) decoder_1 (
    .out1(decoder_1_out1), .out2(decoder_1_out2), .out3(decoder_1_out3), .out4(decoder_1_out4),
    .out5(decoder_1_out5), .out6(decoder_1_out6), .out7(decoder_1_out7), .out8(decoder_1_out8),
    .out9(decoder_1_out9), .out10(decoder_1_out10), .out11(decoder_1_out11), .out12(decoder_1_out12),
    .out13(decoder_1_out13), .out14(decoder_1_out14), .out15(decoder_1_out15), .out16(decoder_1_out16),
    .out17(decoder_1_out17), .out18(decoder_1_out18), .out19(decoder_1_out19), .out20(decoder_1_out20),
    .out21(decoder_1_out21), .out22(decoder_1_out22), .out23(decoder_1_out23), .out24(decoder_1_out24),
    .out25(decoder_1_out25), .out26(decoder_1_out26), .out27(decoder_1_out27), .out28(decoder_1_out28),
    .out29(decoder_1_out29), .out30(decoder_1_out30), .out31(decoder_1_out31), .sel(Rd5Bit));  // open: out0, en

  // Other names for the same wires on the sheet: BusW[31:0] = Data2Reg; Clk = Clock; RA[4:0] = Rs5Bit;
  //   RB[4:0] = Rt5Bit
endmodule
