// Logisim project CompletedDatapath32Bits.circ as structural Verilog: 1 circuit, main circuit DatapathNoCU
module DatapathNoCU (
  input  Jump,
  input  BranchSCR,
  input  [2:0] in_3,
  input  RegWrite,
  input  MemToReg,
  input  ALUScr,
  input  in_7,
  input  [31:0] in_8,
  input  MemWrite,
  input  MemRead,
  input  OpExt,
  output [5:0] out_12,
  output [4:0] out_13,
  output [5:0] out_14
);

  wire CLK, switch_1_p2;
  wire [4:0] codememory_1_fetchedinstruction, codememory_1_fetchedinstruction_2,
       codememory_1_fetchedinstruction_3, multiplexer_2_out;
  wire [15:0] adder_1_out, adder_1_out_2, alu32bitnew_1_result32bits, alu32bitnew_1_result32bits_2;
  wire [27:0] jumpshiftby2bits_1_jump28bitsoutput;
  wire [31:0] adder_2_out, concatenator_1_jumpaddress32bits, datamemory_1_readdata32bitsout,
       leftshifterby2bits_1_imm32bitsshitedby2bits, multiplexer_3_out, multiplexer_4_out, multiplexer_5_out,
       programcounter_1_p1, rigisters_1_rd1, rigisters_1_rd2, signextender_1_immed16to32bits, switch_1_p5;

  Clock clock_1 (.out(CLK));
  // Switch switch_1: pin names not known; wires that end beside it: 1'b1, switch_1_p2, switch_1_p2, CLK, switch_1_p5
  // Probe on {out_14, out_13, codememory_1_fetchedinstruction_2, codememory_1_fetchedinstruction_3, codememory_1_fetchedinstruction, out_12}
  // ProgramCounter programcounter_1: pin names not known; wires that end beside it: programcounter_1_p1
  // Probe on {adder_1_out_2, adder_1_out}
  CodeMemory codememory_1 (
    .AddressA0toA15(adder_1_out),
    .FetchedInstruction({out_14, out_13, codememory_1_fetchedinstruction_2, codememory_1_fetchedinstruction_3, codememory_1_fetchedinstruction, out_12}));
  Adder #(.width(32)) adder_1 (
    .a(in_8), .b(programcounter_1_p1), .out({adder_1_out_2, adder_1_out}), .cin(1'b0));  // open: cout
  JumpShiftBy2Bits jumpshiftby2bits_1 (
    .Imm26BitsIn({out_13, codememory_1_fetchedinstruction_2, codememory_1_fetchedinstruction_3, codememory_1_fetchedinstruction, out_12}),
    .Jump28BitsOutput(jumpshiftby2bits_1_jump28bitsoutput));
  // Probe on {adder_1_out_2, adder_1_out}
  // Probe on switch_1_p5
  Concatenator concatenator_1 (
    .Offset28Bits(jumpshiftby2bits_1_jump28bitsoutput), .PC28to31(adder_1_out_2[15:12]),
    .JumpAddress32Bits(concatenator_1_jumpaddress32bits));
  Multiplexer #(.width(32)) multiplexer_1 (
    .in0(multiplexer_4_out), .in1(concatenator_1_jumpaddress32bits), .out(switch_1_p5), .sel(Jump));
  Multiplexer #(.width(5)) multiplexer_2 (
    .in0(codememory_1_fetchedinstruction_3), .in1(codememory_1_fetchedinstruction_2),
    .out(multiplexer_2_out), .sel(in_7));
  // Probe on {out_14, out_13, codememory_1_fetchedinstruction_2, codememory_1_fetchedinstruction_3, codememory_1_fetchedinstruction, out_12}
  // Probe on rigisters_1_rd1
  // Probe on rigisters_1_rd2
  Rigisters rigisters_1 (
    .RegWrite(RegWrite), .Data2Reg(multiplexer_5_out), .Clock(CLK), .Rs5Bit(codememory_1_fetchedinstruction),
    .Rt5Bit(codememory_1_fetchedinstruction_3), .Rd5Bit(multiplexer_2_out), .RD1(rigisters_1_rd1),
    .RD2(rigisters_1_rd2));
  SignExtender signextender_1 (
    .OpExt(OpExt),
    .Instr0to15Bits({codememory_1_fetchedinstruction_3, codememory_1_fetchedinstruction, out_12}),
    .Immed16to32Bits(signextender_1_immed16to32bits));
  Multiplexer #(.width(32)) multiplexer_3 (
    .in0(rigisters_1_rd2), .in1(signextender_1_immed16to32bits), .out(multiplexer_3_out), .sel(ALUScr));
  // Probe on leftshifterby2bits_1_imm32bitsshitedby2bits
  LeftShifterBy2Bits leftshifterby2bits_1 (
    .Imm32BitsIn(signextender_1_immed16to32bits),
    .Imm32BitsShitedBy2Bits(leftshifterby2bits_1_imm32bitsshitedby2bits));
  // Probe on multiplexer_4_out
  Adder #(.width(32)) adder_2 (
    .a({adder_1_out_2, adder_1_out}), .b(leftshifterby2bits_1_imm32bitsshitedby2bits), .out(adder_2_out),
    .cin(1'b0));  // open: cout
  // Probe on adder_2_out
  // Probe on {alu32bitnew_1_result32bits_2, alu32bitnew_1_result32bits}
  Multiplexer #(.width(32)) multiplexer_4 (
    .in0({adder_1_out_2, adder_1_out}), .in1(adder_2_out), .out(multiplexer_4_out), .sel(BranchSCR));
  alu32bitnew alu32bitnew_1 (
    .OpCode3bits(in_3), .A32bits(rigisters_1_rd1), .B32bits(multiplexer_3_out),
    .Result32bits({alu32bitnew_1_result32bits_2, alu32bitnew_1_result32bits}));  // open: Carry_Borro_In1bit, Carry_Borro_Out1bit
  // Probe on datamemory_1_readdata32bitsout
  DataMemory datamemory_1 (
    .Address16Bits(alu32bitnew_1_result32bits), .MemWrite(MemWrite), .MemRead(MemRead), .CLK(CLK),
    .WriteData32BitsIn(rigisters_1_rd2), .ReadData32BitsOut(datamemory_1_readdata32bitsout));
  Multiplexer #(.width(32)) multiplexer_5 (
    .in0(datamemory_1_readdata32bitsout), .in1({alu32bitnew_1_result32bits_2, alu32bitnew_1_result32bits}),
    .out(multiplexer_5_out), .sel(MemToReg));
endmodule
