// Logisim project CompletedDatapath32BitsWithACU&MCU.circ as structural Verilog: 1 circuit, main circuit DatapathNoCU
module DatapathNoCU (
  input  [31:0] in_1,
  input  OpExt,
  output [5:0] out_3,
  output [4:0] out_4,
  output [5:0] out_5
);

  wire alu32bity_1_zero, and_1_out, CLK, mcu_1_alusrc, mcu_1_branch, mcu_1_jump, mcu_1_memread,
       mcu_1_memtoreg, mcu_1_memwrite, mcu_1_regdst, mcu_1_regwrite, switch_1_p2;
  wire [1:0] mcu_1_aluop2bits;
  wire [3:0] acu_1_operation;
  wire [4:0] codememory_1_fetchedinstruction, codememory_1_fetchedinstruction_2,
       codememory_1_fetchedinstruction_3, multiplexer_2_out;
  wire [15:0] adder_1_out, adder_1_out_2, alu32bity_1_result, alu32bity_1_result_2;
  wire [27:0] jumpshiftby2bits_1_jump28bitsoutput;
  wire [31:0] adder_2_out, concatenator_1_jumpaddress32bits, datamemory_1_readdata32bitsout,
       leftshifterby2bits_1_imm32bitsshitedby2bits, multiplexer_3_out, multiplexer_4_out, multiplexer_5_out,
       programcounter_1_p1, rigisters_1_rd1, rigisters_1_rd2, signextender_1_immed16to32bits, switch_1_p5;

  Clock clock_1 (.out(CLK));
  // Switch switch_1: pin names not known; wires that end beside it: 1'b1, switch_1_p2, switch_1_p2, CLK, switch_1_p5
  // Probe on {out_5, out_4, codememory_1_fetchedinstruction_2, codememory_1_fetchedinstruction_3, codememory_1_fetchedinstruction, out_3}
  // ProgramCounter programcounter_1: pin names not known; wires that end beside it: programcounter_1_p1
  // Probe on {adder_1_out_2, adder_1_out}
  CodeMemory codememory_1 (
    .AddressA0toA15(adder_1_out),
    .FetchedInstruction({out_5, out_4, codememory_1_fetchedinstruction_2, codememory_1_fetchedinstruction_3, codememory_1_fetchedinstruction, out_3}));
  Adder #(.width(32)) adder_1 (
    .a(in_1), .b(programcounter_1_p1), .out({adder_1_out_2, adder_1_out}), .cin(1'b0));  // open: cout
  JumpShiftBy2Bits jumpshiftby2bits_1 (
    .Imm26BitsIn({out_4, codememory_1_fetchedinstruction_2, codememory_1_fetchedinstruction_3, codememory_1_fetchedinstruction, out_3}),
    .Jump28BitsOutput(jumpshiftby2bits_1_jump28bitsoutput));
  // Probe on {adder_1_out_2, adder_1_out}
  // Probe on switch_1_p5
  Concatenator concatenator_1 (
    .Offset28Bits(jumpshiftby2bits_1_jump28bitsoutput), .PC28to31(adder_1_out_2[15:12]),
    .JumpAddress32Bits(concatenator_1_jumpaddress32bits));
  MCU mcu_1 (
    .In6bitsOpCode(out_3), .RegDst(mcu_1_regdst), .Jump(mcu_1_jump), .ALUSrc(mcu_1_alusrc),
    .MemtoReg(mcu_1_memtoreg), .RegWrite(mcu_1_regwrite), .MemRead(mcu_1_memread), .MemWrite(mcu_1_memwrite),
    .Branch(mcu_1_branch), .ALUOp2bits(mcu_1_aluop2bits));
  // Probe on {out_5, out_4, codememory_1_fetchedinstruction_2, codememory_1_fetchedinstruction_3, codememory_1_fetchedinstruction, out_3}
  Multiplexer #(.width(32)) multiplexer_1 (
    .in0(multiplexer_4_out), .in1(concatenator_1_jumpaddress32bits), .out(switch_1_p5), .sel(mcu_1_jump));
  Multiplexer #(.width(5)) multiplexer_2 (
    .in0(codememory_1_fetchedinstruction_3), .in1(codememory_1_fetchedinstruction_2),
    .out(multiplexer_2_out), .sel(mcu_1_regdst));
  // Probe on rigisters_1_rd1
  // Probe on rigisters_1_rd2
  Rigisters rigisters_1 (
    .RegWrite(mcu_1_regwrite), .Data2Reg(multiplexer_5_out), .Clock(CLK),
    .Rs5Bit(codememory_1_fetchedinstruction), .Rt5Bit(codememory_1_fetchedinstruction_3),
    .Rd5Bit(multiplexer_2_out), .RD1(rigisters_1_rd1), .RD2(rigisters_1_rd2));
  SignExtender signextender_1 (
    .OpExt(OpExt),
    .Instr0to15Bits({codememory_1_fetchedinstruction_3, codememory_1_fetchedinstruction, out_3}),
    .Immed16to32Bits(signextender_1_immed16to32bits));
  Multiplexer #(.width(32)) multiplexer_3 (
    .in0(rigisters_1_rd2), .in1(signextender_1_immed16to32bits), .out(multiplexer_3_out), .sel(mcu_1_alusrc));
  ACU acu_1 (.ALUOp(mcu_1_aluop2bits), .F6bits0to5(out_5), .Operation(acu_1_operation));
  // Probe on leftshifterby2bits_1_imm32bitsshitedby2bits
  LeftShifterBy2Bits leftshifterby2bits_1 (
    .Imm32BitsIn(signextender_1_immed16to32bits),
    .Imm32BitsShitedBy2Bits(leftshifterby2bits_1_imm32bitsshitedby2bits));
  // Probe on {alu32bity_1_result_2, alu32bity_1_result}
  ALU32Bity alu32bity_1 (
    .OpCode4Bits(acu_1_operation), .Ainput(rigisters_1_rd1), .Binput(multiplexer_3_out),
    .Result({alu32bity_1_result_2, alu32bity_1_result}), .Zero(alu32bity_1_zero));
  and and_1 (and_1_out, mcu_1_branch, alu32bity_1_zero);
  Adder #(.width(32)) adder_2 (
    .a({adder_1_out_2, adder_1_out}), .b(leftshifterby2bits_1_imm32bitsshitedby2bits), .out(adder_2_out),
    .cin(1'b0));  // open: cout
  Multiplexer #(.width(32)) multiplexer_4 (
    .in0({adder_1_out_2, adder_1_out}), .in1(adder_2_out), .out(multiplexer_4_out), .sel(and_1_out));
  // Probe on adder_2_out
  // Probe on multiplexer_4_out
  // Probe on datamemory_1_readdata32bitsout
  DataMemory datamemory_1 (
    .Address16Bits(alu32bity_1_result), .MemWrite(mcu_1_memwrite), .MemRead(mcu_1_memread), .CLK(CLK),
    .WriteData32BitsIn(rigisters_1_rd2), .ReadData32BitsOut(datamemory_1_readdata32bitsout));
  Multiplexer #(.width(32)) multiplexer_5 (
    .in0(datamemory_1_readdata32bitsout), .in1({alu32bity_1_result_2, alu32bity_1_result}),
    .out(multiplexer_5_out), .sel(mcu_1_memtoreg));

  // Notes on the sheet:
  //   RegDst
  //   Jump
  //   ALUSrc
  //   MemWrite
  //   BranchSCR
  //   MemRead
endmodule
