// Logisim project NewALU1bit.circ as structural Verilog: 1 circuit, main circuit alu1bitnew
module alu1bitnew (
  input  A1bit,
  input  B1bit,
  input  Carry_Borro_In1bit,
  input  [2:0] OpCode3bits,
  output Result1bit,
  output Cout,
  output Bout
);

  wire adder_1_out, AND1_out, NAND1_out, NOR1_out, OR1_out, subtractor_1_out, XNOR1_out, XOR1_out;

  and AND1 (AND1_out, B1bit, A1bit);
  nand NAND1 (NAND1_out, B1bit, A1bit);
  or OR1 (OR1_out, B1bit, A1bit);
  nor NOR1 (NOR1_out, B1bit, A1bit);
  xor XOR1 (XOR1_out, B1bit, A1bit);
  xnor XNOR1 (XNOR1_out, B1bit, A1bit);
  Adder #(.width(1)) adder_1 (.a(B1bit), .b(A1bit), .out(adder_1_out), .cin(Carry_Borro_In1bit), .cout(Cout));
  Subtractor #(.width(1)) subtractor_1 (
    .a(B1bit), .b(A1bit), .out(subtractor_1_out), .bin(Carry_Borro_In1bit), .bout(Bout));
  Multiplexer #(.select(3)) multiplexer_1 (
    .in0(AND1_out), .in1(NAND1_out), .in2(OR1_out), .in3(NOR1_out), .in4(XOR1_out), .in5(XNOR1_out),
    .in6(adder_1_out), .in7(subtractor_1_out), .out(Result1bit), .sel(OpCode3bits));
endmodule
