// Logisim project NewALU32bit.circ as structural Verilog: 1 circuit, main circuit alu32bitnew
module alu32bitnew (
  input  [2:0] OpCode3bits,
  input  Carry_Borro_In1bit,
  input  [31:0] A32bits,
  input  [31:0] B32bits,
  output [31:0] Result32bits,
  output Carry_Borro_Out1bit
);

  wire alu4bitnew_1_carry_borro_out1bit, alu4bitnew_2_carry_borro_out1bit, alu4bitnew_3_carry_borro_out1bit,
       alu4bitnew_4_carry_borro_out1bit, alu4bitnew_5_carry_borro_out1bit, alu4bitnew_6_carry_borro_out1bit,
       alu4bitnew_7_carry_borro_out1bit;

  alu4bitnew alu4bitnew_1 (
    .OpCode3bits(OpCode3bits), .A4bits(A32bits[3:0]), .B4bits(B32bits[3:0]),
    .Carry_Borro_In1bit(Carry_Borro_In1bit), .Result4bits(Result32bits[3:0]),
    .Carry_Borro_Out1bit(alu4bitnew_1_carry_borro_out1bit));
  alu4bitnew alu4bitnew_2 (
    .OpCode3bits(OpCode3bits), .A4bits(A32bits[7:4]), .B4bits(B32bits[7:4]),
    .Carry_Borro_In1bit(alu4bitnew_1_carry_borro_out1bit), .Result4bits(Result32bits[7:4]),
    .Carry_Borro_Out1bit(alu4bitnew_2_carry_borro_out1bit));
  alu4bitnew alu4bitnew_3 (
    .OpCode3bits(OpCode3bits), .A4bits(A32bits[11:8]), .B4bits(B32bits[11:8]),
    .Carry_Borro_In1bit(alu4bitnew_2_carry_borro_out1bit), .Result4bits(Result32bits[11:8]),
    .Carry_Borro_Out1bit(alu4bitnew_3_carry_borro_out1bit));
  alu4bitnew alu4bitnew_4 (
    .OpCode3bits(OpCode3bits), .A4bits(A32bits[15:12]), .B4bits(B32bits[15:12]),
    .Carry_Borro_In1bit(alu4bitnew_3_carry_borro_out1bit), .Result4bits(Result32bits[15:12]),
    .Carry_Borro_Out1bit(alu4bitnew_4_carry_borro_out1bit));
  alu4bitnew alu4bitnew_5 (
    .OpCode3bits(OpCode3bits), .A4bits(A32bits[19:16]), .B4bits(B32bits[19:16]),
    .Carry_Borro_In1bit(alu4bitnew_4_carry_borro_out1bit), .Result4bits(Result32bits[19:16]),
    .Carry_Borro_Out1bit(alu4bitnew_5_carry_borro_out1bit));
  alu4bitnew alu4bitnew_6 (
    .OpCode3bits(OpCode3bits), .A4bits(A32bits[23:20]), .B4bits(B32bits[23:20]),
    .Carry_Borro_In1bit(alu4bitnew_5_carry_borro_out1bit), .Result4bits(Result32bits[23:20]),
    .Carry_Borro_Out1bit(alu4bitnew_6_carry_borro_out1bit));
  alu4bitnew alu4bitnew_7 (
    .OpCode3bits(OpCode3bits), .A4bits(A32bits[27:24]), .B4bits(B32bits[27:24]),
    .Carry_Borro_In1bit(alu4bitnew_6_carry_borro_out1bit), .Result4bits(Result32bits[27:24]),
    .Carry_Borro_Out1bit(alu4bitnew_7_carry_borro_out1bit));
  alu4bitnew alu4bitnew_8 (
    .OpCode3bits(OpCode3bits), .A4bits(A32bits[31:28]), .B4bits(B32bits[31:28]),
    .Carry_Borro_In1bit(alu4bitnew_7_carry_borro_out1bit), .Result4bits(Result32bits[31:28]),
    .Carry_Borro_Out1bit(Carry_Borro_Out1bit));
endmodule
