// Logisim project NewALU4bits.circ as structural Verilog: 1 circuit, main circuit alu4bitnew
module alu4bitnew (
  input  [2:0] OpCode3bits,
  input  [3:0] A4bits,
  input  [3:0] B4bits,
  input  Carry_Borro_In1bit,
  output [3:0] Result4bits,
  output Carry_Borro_Out1bit
);

  wire alu1bitnew_1_bout, alu1bitnew_1_cout, alu1bitnew_2_bout, alu1bitnew_2_cout, alu1bitnew_3_bout,
       alu1bitnew_3_cout, alu1bitnew_4_bout, alu1bitnew_4_cout, multiplexer_1_out, multiplexer_2_out,
       multiplexer_3_out;

  alu1bitnew alu1bitnew_1 (
    .A1bit(A4bits[0]), .B1bit(B4bits[0]), .Carry_Borro_In1bit(Carry_Borro_In1bit), .OpCode3bits(OpCode3bits),
    .Result1bit(Result4bits[0]), .Cout(alu1bitnew_1_cout), .Bout(alu1bitnew_1_bout));
  alu1bitnew alu1bitnew_2 (
    .A1bit(A4bits[1]), .B1bit(B4bits[1]), .Carry_Borro_In1bit(multiplexer_1_out), .OpCode3bits(OpCode3bits),
    .Result1bit(Result4bits[1]), .Cout(alu1bitnew_2_cout), .Bout(alu1bitnew_2_bout));
  alu1bitnew alu1bitnew_3 (
    .A1bit(A4bits[2]), .B1bit(B4bits[2]), .Carry_Borro_In1bit(multiplexer_2_out), .OpCode3bits(OpCode3bits),
    .Result1bit(Result4bits[2]), .Cout(alu1bitnew_3_cout), .Bout(alu1bitnew_3_bout));
  alu1bitnew alu1bitnew_4 (
    .A1bit(A4bits[3]), .B1bit(B4bits[3]), .Carry_Borro_In1bit(multiplexer_3_out), .OpCode3bits(OpCode3bits),
    .Result1bit(Result4bits[3]), .Cout(alu1bitnew_4_cout), .Bout(alu1bitnew_4_bout));
  Multiplexer multiplexer_1 (
    .in0(alu1bitnew_1_cout), .in1(alu1bitnew_1_bout), .out(multiplexer_1_out), .sel(OpCode3bits[0]));
  Multiplexer multiplexer_2 (
    .in0(alu1bitnew_2_cout), .in1(alu1bitnew_2_bout), .out(multiplexer_2_out), .sel(OpCode3bits[0]));
  Multiplexer multiplexer_3 (
    .in0(alu1bitnew_3_cout), .in1(alu1bitnew_3_bout), .out(multiplexer_3_out), .sel(OpCode3bits[0]));
  Multiplexer multiplexer_4 (
    .in0(alu1bitnew_4_cout), .in1(alu1bitnew_4_bout), .out(Carry_Borro_Out1bit), .sel(OpCode3bits[0]));
endmodule
