// Logisim project OtherPartsOfDatapath32Bits.circ as structural Verilog: 2 circuits, main circuit CodeMemory
module CodeMemory (
  input  [15:0] AddressA0toA15,
  output [31:0] FetchedInstruction
);

  ROM #(.addrWidth(16), .dataWidth(32)) rom_1 (.addr(AddressA0toA15), .data(FetchedInstruction));
endmodule

module DataMemory (
  input  [15:0] Address16Bits,
  input  MemWrite,
  input  MemRead,
  input  CLK,
  input  [31:0] WriteData32BitsIn,
  output [31:0] ReadData32BitsOut
);

  RAM #(.addrWidth(16), .dataWidth(32)) ram_1 (
    .addr(Address16Bits), .we(MemWrite), .oe(MemRead), .clk(CLK), .din(WriteData32BitsIn),
    .dout(ReadData32BitsOut));
endmodule
