// Logisim project PC22176.circ as structural Verilog: 1 circuit, main circuit ProgramCounter
module ProgramCounter (
  input  SetButton,
  input  CLK,
  input  [31:0] PCinput32bits,
  output [31:0] PCout
);

  wire [31:0] adder_1_out, counter_1_q;

  Counter #(.max('hffffffff), .width(32)) counter_1 (
    .clr(SetButton), .clk(CLK), .D(adder_1_out), .Q(counter_1_q));  // open: load, up, count, carry
  Pull_Resistor pull_resistor_1 (.node(SetButton));
  Adder #(.width(32)) adder_1 (.a(PCinput32bits), .b(counter_1_q), .out(adder_1_out));  // open: cin, cout
  ROM #(.addrWidth(16), .dataWidth(32)) rom_1 (.addr(counter_1_q[15:0]), .data(PCout));
endmodule
