// Logisim project PartsOfDatapath32Bits.circ as structural Verilog: 4 circuits, main circuit SignExtender
module SignExtender (
  input  OpExt,
  input  [15:0] Instr0to15Bits,
  output [31:0] Immed16to32Bits
);

  and and_1 (Immed16to32Bits[31], OpExt, Instr0to15Bits[15]);

  assign Immed16to32Bits[30:0] = {{15{Immed16to32Bits[31]}}, Instr0to15Bits};
endmodule

module LeftShifterBy2Bits (
  input  [31:0] Imm32BitsIn,
  output [31:0] Imm32BitsShitedBy2Bits
);


  assign Imm32BitsShitedBy2Bits = {Imm32BitsIn[29:0], 2'b00};

  // Notes on the sheet:
  //   Multiplied by 4
endmodule

module JumpShiftBy2Bits (
  input  [25:0] Imm26BitsIn,
  output [27:0] Jump28BitsOutput
);


  assign Jump28BitsOutput = {Imm26BitsIn, 2'b00};
endmodule

module Concatenator (
  input  [27:0] Offset28Bits,
  input  [3:0] PC28to31,
  output [31:0] JumpAddress32Bits
);


  assign JumpAddress32Bits = {PC28to31, Offset28Bits};
endmodule
