// Logisim project ACUandMCU.circ as structural Verilog: 2 circuits, main circuit ACU
module ACU (
  input  [1:0] ALUOp,
  input  [5:0] F6bits0to5,
  output [3:0] Operation
);

  wire and_1_out, or_1_out;

  or or_1 (or_1_out, F6bits0to5[0], F6bits0to5[3]);
  and and_1 (and_1_out, F6bits0to5[1], ALUOp[1]);
  and Op0 (Operation[0], ALUOp[1], or_1_out);
  or Op1 (Operation[1], ~ALUOp[1], ~F6bits0to5[2]);  // OR_Gate
  or Op2 (Operation[2], ALUOp[0], and_1_out);
  and Op3 (Operation[3], ALUOp[0], ~ALUOp[0]);  // AND_Gate
endmodule

module MCU (
  input  [5:0] In6bitsOpCode,
  output RegDst,
  output Jump,
  output ALUSrc,
  output MemtoReg,
  output RegWrite,
  output MemRead,
  output MemWrite,
  output Branch,
  output [1:0] ALUOp2bits
);

  and and_1 (Jump, ~In6bitsOpCode[5], ~In6bitsOpCode[4], ~In6bitsOpCode[3], ~In6bitsOpCode[2], In6bitsOpCode[1], ~In6bitsOpCode[0]);  // AND_Gate
  and Rformat (ALUOp2bits[1], ~In6bitsOpCode[5], ~In6bitsOpCode[4], ~In6bitsOpCode[3], ~In6bitsOpCode[2], ~In6bitsOpCode[1], ~In6bitsOpCode[0]);  // AND_Gate
  and LW (MemRead, In6bitsOpCode[5], ~In6bitsOpCode[4], ~In6bitsOpCode[3], ~In6bitsOpCode[2], In6bitsOpCode[1], In6bitsOpCode[0]);  // AND_Gate
  and SW (MemWrite, In6bitsOpCode[5], ~In6bitsOpCode[4], In6bitsOpCode[3], ~In6bitsOpCode[2], In6bitsOpCode[1], In6bitsOpCode[0]);  // AND_Gate
  and BEQ (ALUOp2bits[0], ~In6bitsOpCode[5], ~In6bitsOpCode[4], ~In6bitsOpCode[3], In6bitsOpCode[2], ~In6bitsOpCode[1], ~In6bitsOpCode[0]);  // AND_Gate
  or or_1 (ALUSrc, MemRead, MemWrite);
  or or_2 (RegWrite, ALUOp2bits[1], MemRead);
  LED ALUOp1 (.in(ALUOp2bits[1]));
  LED ALUOp0 (.in(ALUOp2bits[0]));

  assign Branch = ALUOp2bits[0];
  assign MemtoReg = MemRead;
  assign RegDst = ALUOp2bits[1];
endmodule
