// Logisim project ALU32Bityz.circ as structural Verilog: 3 circuits, main circuit ALU1Bity
module ALU1Bity (
  input  [1:0] OpCode2bits,
  input  Ainput,
  input  Binput,
  input  Ainv,
  input  Binv,
  input  Carry_Borro_In1bit,
  input  Less,
  output Result,
  output Cout,
  output Set
);

  wire and_1_out, multiplexer_1_out, multiplexer_2_out, not_1_out, not_2_out, or_1_out;

  not not_1 (not_1_out, Ainput);
  not not_2 (not_2_out, Binput);
  Multiplexer multiplexer_1 (.in0(Ainput), .in1(not_1_out), .out(multiplexer_1_out), .sel(Ainv));
  Multiplexer multiplexer_2 (.in0(Binput), .in1(not_2_out), .out(multiplexer_2_out), .sel(Binv));
  and and_1 (and_1_out, multiplexer_1_out, multiplexer_2_out);
  or or_1 (or_1_out, multiplexer_1_out, multiplexer_2_out);
  Adder #(.width(1)) adder_1 (
    .a(multiplexer_1_out), .b(multiplexer_2_out), .out(Set), .cin(Carry_Borro_In1bit), .cout(Cout));
  Multiplexer #(.select(2)) multiplexer_3 (
    .in0(and_1_out), .in1(or_1_out), .in2(Set), .in3(Less), .out(Result), .sel(OpCode2bits));
endmodule

module ALU4Bity (
  input  [3:0] OpCode4Bits,
  input  [3:0] Ainput,
  input  [3:0] Binput,
  input  Carry_Borro_In1bit,
  input  Less,
  output [3:0] Result,
  output Cout,
  output Set
);

  wire alu1bity_1_cout, alu1bity_2_cout, alu1bity_3_cout;

  ALU1Bity alu1bity_1 (
    .OpCode2bits(OpCode4Bits[1:0]), .Ainput(Ainput[0]), .Binput(Binput[0]), .Ainv(OpCode4Bits[3]),
    .Binv(OpCode4Bits[2]), .Carry_Borro_In1bit(Carry_Borro_In1bit), .Less(Less), .Result(Result[0]),
    .Cout(alu1bity_1_cout));  // open: Set
  ALU1Bity alu1bity_2 (
    .OpCode2bits(OpCode4Bits[1:0]), .Ainput(Ainput[1]), .Binput(Binput[1]), .Ainv(OpCode4Bits[3]),
    .Binv(OpCode4Bits[2]), .Carry_Borro_In1bit(alu1bity_1_cout), .Less(1'b0), .Result(Result[1]),
    .Cout(alu1bity_2_cout));  // open: Set
  ALU1Bity alu1bity_3 (
    .OpCode2bits(OpCode4Bits[1:0]), .Ainput(Ainput[2]), .Binput(Binput[2]), .Ainv(OpCode4Bits[3]),
    .Binv(OpCode4Bits[2]), .Carry_Borro_In1bit(alu1bity_2_cout), .Less(1'b0), .Result(Result[2]),
    .Cout(alu1bity_3_cout));  // open: Set
  ALU1Bity alu1bity_4 (
    .OpCode2bits(OpCode4Bits[1:0]), .Ainput(Ainput[3]), .Binput(Binput[3]), .Ainv(OpCode4Bits[3]),
    .Binv(OpCode4Bits[2]), .Carry_Borro_In1bit(alu1bity_3_cout), .Less(1'b0), .Result(Result[3]),
    .Cout(Cout), .Set(Set));
endmodule

module ALU32Bity (
  input  [3:0] OpCode4Bits,
  input  [31:0] Ainput,
  input  [31:0] Binput,
  output [31:0] Result,
  output Zero
);

  wire eight_set, five_cout, four_cout, one_cout, or_1_out, seven_cout, six_cout, three_cout, two_cout;

  ALU4Bity one (
    .OpCode4Bits(OpCode4Bits), .Ainput(Ainput[3:0]), .Binput(Binput[3:0]),
    .Carry_Borro_In1bit(OpCode4Bits[2]), .Less(eight_set), .Result(Result[3:0]), .Cout(one_cout));  // open: Set
  ALU4Bity two (
    .OpCode4Bits(OpCode4Bits), .Ainput(Ainput[7:4]), .Binput(Binput[7:4]), .Carry_Borro_In1bit(one_cout),
    .Less(1'b0), .Result(Result[7:4]), .Cout(two_cout));  // open: Set
  ALU4Bity three (
    .OpCode4Bits(OpCode4Bits), .Ainput(Ainput[11:8]), .Binput(Binput[11:8]), .Carry_Borro_In1bit(two_cout),
    .Less(1'b0), .Result(Result[11:8]), .Cout(three_cout));  // open: Set
  ALU4Bity four (
    .OpCode4Bits(OpCode4Bits), .Ainput(Ainput[15:12]), .Binput(Binput[15:12]),
    .Carry_Borro_In1bit(three_cout), .Less(1'b0), .Result(Result[15:12]), .Cout(four_cout));  // open: Set
  ALU4Bity five (
    .OpCode4Bits(OpCode4Bits), .Ainput(Ainput[19:16]), .Binput(Binput[19:16]),
    .Carry_Borro_In1bit(four_cout), .Less(1'b0), .Result(Result[19:16]), .Cout(five_cout));  // open: Set
  ALU4Bity six (
    .OpCode4Bits(OpCode4Bits), .Ainput(Ainput[23:20]), .Binput(Binput[23:20]),
    .Carry_Borro_In1bit(five_cout), .Less(1'b0), .Result(Result[23:20]), .Cout(six_cout));  // open: Set
  ALU4Bity seven (
    .OpCode4Bits(OpCode4Bits), .Ainput(Ainput[27:24]), .Binput(Binput[27:24]), .Carry_Borro_In1bit(six_cout),
    .Less(1'b0), .Result(Result[27:24]), .Cout(seven_cout));  // open: Set
  ALU4Bity eight (
    .OpCode4Bits(OpCode4Bits), .Ainput(Ainput[31:28]), .Binput(Binput[31:28]),
    .Carry_Borro_In1bit(seven_cout), .Less(1'b0), .Result(Result[31:28]), .Set(eight_set));  // open: Cout
  or or_1 (or_1_out, Result[16], Result[17], Result[18], Result[19], Result[20], Result[21], Result[22], Result[23], Result[24], Result[25], Result[26], Result[27], Result[28], Result[29], Result[30], Result[31], Result[0], Result[1], Result[2], Result[3], Result[4], Result[5], Result[6], Result[7], Result[8], Result[9], Result[10], Result[11], Result[12], Result[13], Result[14], Result[15]);
  not not_1 (Zero, or_1_out);
endmodule
