// Logisim project lab7.circ as structural Verilog: 1 circuit, main circuit RCA32bit
module RCA32bit (
  input  [31:0] InputA,
  input  [31:0] InputB,
  output [31:0] S,
  output CarryOut
);

  wire fa1_1_p4, fa1_2_p4, fa1_3_p4;

  // FA1 fa1_1: pin names not known; wires that end beside it: InputA[7:0], InputB[7:0], 1'b0, fa1_1_p4, S[7:0]
  // FA1 fa1_2: pin names not known; wires that end beside it: InputA[15:8], InputB[15:8], fa1_1_p4, fa1_2_p4, S[15:8]
  // FA1 fa1_3: pin names not known; wires that end beside it: InputA[23:16], InputB[23:16], fa1_2_p4, fa1_3_p4, S[23:16]
  // FA1 fa1_4: pin names not known; wires that end beside it: InputA[31:24], InputB[31:24], fa1_3_p4, CarryOut, S[31:24]
  LED LedGreanRed (.in(CarryOut));
endmodule
