// Logisim project lab8a.circ as structural Verilog: 1 circuit, main circuit main
module main (
  input  [7:0] in_1,
  output out_2
);

  wire button_1_out, button_2_out, clock_1_out, switch_1_p2, switch_2_p2;
  wire [7:0] counter_1_q;

  // Switch switch_1: pin names not known; wires that end beside it: 1'b1, switch_1_p2
  // Switch switch_2: pin names not known; wires that end beside it: 1'b1, switch_2_p2
  Pull_Resistor pull_resistor_1 (.node(switch_1_p2));
  Button button_1 (.out(button_1_out));
  Button button_2 (.out(button_2_out));
  Pull_Resistor pull_resistor_2 (.node(switch_2_p2));
  Clock clock_1 (.out(clock_1_out));
  Counter counter_1 (
    .clr(button_1_out), .load(button_2_out), .up(switch_2_p2), .count(switch_1_p2), .clk(clock_1_out),
    .D(in_1), .carry(out_2), .Q(counter_1_q));
  LedBar ledbar_1 (
    .led0(counter_1_q[0]), .led1(counter_1_q[1]), .led2(counter_1_q[2]), .led3(counter_1_q[3]),
    .led4(counter_1_q[4]), .led5(counter_1_q[5]), .led6(counter_1_q[6]), .led7(counter_1_q[7]));
  LED led_1 (.in(out_2));
endmodule
